# Fritzing sketch NRF8001_Bluetooth (saved by Fritzing 0.9.3b)
breadboards: 1

parts:
  Part1 = Adafruit nRF8001 Breakout [part_number="Adafruit #1697"]
  Part2 = Arduino Uno (Rev3)

nets:
  N1: Part1.SCK, Part2.D13/SCK
  N2: Part1.MISO, Part2.D12/MISO
  N3: Part1.MOSI, Part2.D11_PWM/MOSI
  N4: Part1.REQN, Part2.D10_PWM/SS
  N5: Part1.RDYN, Part2.D2
  N6: Part1.RESET, Part2.D9_PWM
  GND: Part1.GND, Part2.GND
  VIN: Part1.VIN, Part2.5V

custom parts:
  Adafruit nRF8001 Breakout: Our Adafruit Bluefruit LE (Bluetooth Smart, Bluetooth Low Energy, Bluetooth 4.0) nRF8001 Breakout allows you to establish an easy to use wireless link between your Arduino and any compatible iOS or Android (4.3+) device. It works by simulating a UART device beneath the surface, sending ASCII data back and forth between the devices, letting you decide what data to send and what to do with it on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
