# Fritzing sketch ShutterControl (saved by Fritzing 0.9.3b)
breadboards: 1

parts:
  Part1 = Arduino Uno (Rev3) - ICSP
  Part2 = USB Mini-B Breakout [part_number=1764]
  Q1 = NPN-Transistor [package="TO92 [THT]"]

nets:
  N1: Part1.D2, Q1.C
  GND: Part1.GND, Part2.GND, Q1.E
  N2: Part2.ID, Q1.B

custom parts:
  USB Mini-B Breakout: Simple but effective - this breakout board has a USB Mini-B connector, with all 5 pins broken out. Great for pairing with a microcontroller with USB support, or adding USB 5V power to a project.
